# Fritzing sketch Untitled Sketch (saved by Fritzing 0.9.3b)
breadboards: 1

parts:
  元件1 = Arduino Uno (Rev3)
  PIR = IR Receiver Breakout [package=PCB]
  红外信号发射端 = TSOP312.., 314.. [package=THT]

nets:
  N1: 元件1.D2, PIR.OUT
  N2: 元件1.D4, 红外信号发射端.Vs
  5V: 元件1.5V, PIR.VCC, 红外信号发射端.Data
  GND: 元件1.GND, PIR.GND, 红外信号发射端.GND
